// Logisim project logisim file.circ as structural Verilog: 3 circuits, main circuit main
// A'
module main (
);

  wire A_q, A_qn, and_1_out, and_2_out, and_3_out, and_4_out, B_q, B_qn, C_q, C_qn, clock_1_out, D_q, D_qn,
       or_1_out, or_2_out, or_3_out, or_4_out;

  Clock clock_1 (.out(clock_1_out));
  T_Flip_Flop #(.trigger("falling")) A (.clk(B_q), .T(1'b1), .Q(A_q), .Qn(A_qn));  // open: preset, reset, en
  T_Flip_Flop #(.trigger("falling")) B (.clk(C_q), .T(1'b1), .Q(B_q), .Qn(B_qn));  // open: preset, reset, en
  T_Flip_Flop #(.trigger("falling")) C (.clk(D_q), .T(1'b1), .Q(C_q), .Qn(C_qn));  // open: preset, reset, en
  T_Flip_Flop #(.trigger("falling")) D (.clk(clock_1_out), .T(1'b1), .Q(D_q), .Qn(D_qn));  // open: preset, reset, en
  or or_1 (or_1_out, A_q, B_q, C_q, D_q);
  LED led_1 (.in(or_1_out));
  and and_1 (and_1_out, A_qn, B_q, C_qn, D_qn);
  and and_2 (and_2_out, A_qn, B_qn, C_q);
  or or_2 (or_2_out, and_1_out, and_2_out, and_3_out);
  LED led_2 (.in(or_2_out));
  and and_3 (and_3_out, A_qn, B_qn, D_q);
  or or_3 (or_3_out, D_q, C_q);
  and and_4 (and_4_out, B_q, or_3_out);
  or or_4 (or_4_out, A_q, and_4_out);
  LED led_3 (.in(or_4_out));

  // Notes on the sheet:
  //   LIGHT
  //   FAN
  //   A
  //   A'
  //   B
  //   B'
  //   Air Condition
  //   C
  //   C'
  //   D
  //   D'
endmodule

module BCD_decoder2 (
  input  A3,
  input  A2,
  input  A1,
  input  A0,
  output g,
  output f,
  output e,
  output d,
  output c,
  output b,
  output a
);

  wire and_1_out, and_2_out, and_3_out, and_4_out, and_5_out, and_6_out, and_7_out, and_8_out, and_9_out,
       and_10_out, and_11_out, and_12_out, and_13_out, and_14_out, and_15_out, and_16_out, and_17_out,
       and_18_out, and_19_out, and_20_out, and_21_out, and_22_out, and_23_out, and_24_out, and_25_out,
       and_26_out, and_27_out, and_28_out, and_29_out, and_30_out, and_31_out, not_1_out, not_2_out,
       not_3_out, not_4_out, not_5_out, not_6_out, not_7_out, not_8_out, not_9_out, not_10_out, not_11_out,
       not_12_out, not_13_out, not_14_out, not_15_out, not_16_out, not_17_out, not_18_out, not_19_out,
       not_20_out, not_21_out, not_22_out, not_23_out, not_24_out, not_25_out, not_26_out, not_27_out,
       not_28_out, not_29_out, not_30_out, not_31_out, not_32_out, not_33_out, not_34_out, not_35_out,
       not_36_out, not_37_out, not_38_out, not_39_out, not_40_out, not_41_out, not_42_out, not_43_out;

  not not_1 (not_1_out, A2);
  and and_1 (and_1_out, not_1_out, not_2_out);
  not not_2 (not_2_out, A0);
  not not_3 (not_3_out, A3);
  and and_2 (and_2_out, not_3_out, A1);
  and and_3 (and_3_out, A2, A0);
  and and_4 (and_4_out, A3, not_4_out);
  not not_4 (not_4_out, A1);
  not not_5 (not_5_out, A2);
  not not_6 (not_6_out, A1);
  and and_5 (and_5_out, not_6_out, not_7_out);
  not not_7 (not_7_out, A0);
  not not_8 (not_8_out, A3);
  and and_6 (and_6_out, not_8_out, A1, A0);
  and and_7 (and_7_out, A3, not_9_out);
  not not_9 (not_9_out, A1);
  and and_8 (and_8_out, A3, not_10_out);
  not not_10 (not_10_out, A0);
  not not_11 (not_11_out, A3);
  and and_9 (and_9_out, not_11_out, not_12_out);
  not not_12 (not_12_out, A1);
  and and_10 (and_10_out, A2, A1);
  and and_11 (and_11_out, A3, not_13_out);
  not not_13 (not_13_out, A2);
  not not_14 (not_14_out, A2);
  and and_12 (and_12_out, not_14_out, not_15_out);
  not not_15 (not_15_out, A0);
  not not_16 (not_16_out, A3);
  not not_17 (not_17_out, A2);
  and and_13 (and_13_out, not_16_out, not_17_out, A1);
  not not_18 (not_18_out, A3);
  and and_14 (and_14_out, not_18_out, A1, not_19_out);
  not not_19 (not_19_out, A0);
  not not_20 (not_20_out, A1);
  and and_15 (and_15_out, A2, not_20_out, A0);
  and and_16 (and_16_out, A3, not_21_out);
  not not_21 (not_21_out, A1);
  and and_17 (and_17_out, A3, A2, A0);
  not not_22 (not_22_out, A2);
  and and_18 (and_18_out, not_22_out, not_23_out);
  not not_23 (not_23_out, A0);
  not not_24 (not_24_out, A3);
  and and_19 (and_19_out, not_24_out, A1, not_25_out);
  not not_25 (not_25_out, A0);
  not not_26 (not_26_out, A1);
  and and_20 (and_20_out, A3, not_26_out, not_27_out);
  not not_27 (not_27_out, A0);
  not not_28 (not_28_out, A3);
  and and_21 (and_21_out, not_28_out, not_29_out, not_30_out);
  not not_29 (not_29_out, A1);
  not not_30 (not_30_out, A0);
  not not_31 (not_31_out, A3);
  and and_22 (and_22_out, not_31_out, A2, not_32_out);
  not not_32 (not_32_out, A1);
  not not_33 (not_33_out, A3);
  and and_23 (and_23_out, not_33_out, A2, not_34_out);
  not not_34 (not_34_out, A0);
  and and_24 (and_24_out, A3, not_35_out, not_36_out);
  not not_35 (not_35_out, A2);
  not not_36 (not_36_out, A1);
  not not_37 (not_37_out, A2);
  and and_25 (and_25_out, A3, not_37_out, not_38_out);
  not not_38 (not_38_out, A0);
  and and_26 (and_26_out, A3, A2, A1);
  not not_39 (not_39_out, A3);
  not not_40 (not_40_out, A2);
  and and_27 (and_27_out, not_39_out, not_40_out, A1);
  and and_28 (and_28_out, A2, not_41_out);
  not not_41 (not_41_out, A1);
  and and_29 (and_29_out, A2, not_42_out);
  not not_42 (not_42_out, A0);
  and and_30 (and_30_out, A3, not_43_out);
  not not_43 (not_43_out, A1);
  and and_31 (and_31_out, A3, A2);
  or or_1 (g, and_1_out, and_2_out, and_3_out, and_4_out);
  or or_2 (f, not_5_out, and_5_out, and_6_out, and_7_out, and_8_out);
  or or_3 (e, and_9_out, A0, and_10_out, and_11_out);
  or or_4 (c, and_18_out, and_19_out, and_20_out);
  or or_5 (a, and_27_out, and_28_out, and_29_out, and_30_out, and_31_out);
  or or_6 (d, and_12_out, and_13_out, and_14_out, and_15_out, and_16_out, and_17_out);
  or or_7 (b, and_21_out, and_22_out, and_23_out, and_24_out, and_25_out, and_26_out);
endmodule

module BCD_decoder (
  input  A3,
  input  A2,
  input  A1,
  input  A0,
  output g,
  output f,
  output e,
  output d,
  output c,
  output b,
  output a
);

  wire and_1_out, and_2_out, and_3_out, and_4_out;

  and and_1 (and_1_out, A3, A1);
  and and_2 (and_2_out, A3, A2);
  and and_3 (and_3_out, A3, A1);
  and and_4 (and_4_out, A3, A2);
  or or_1 (f, and_1_out, and_2_out);
  or or_2 (e, and_3_out, and_4_out);

  assign a = 1'b0;
  assign b = 1'b0;
  assign c = 1'b0;
  assign d = 1'b0;
  assign g = 1'b0;
endmodule
